# Fritzing sketch weathe_station_schematics_pcb (saved by Fritzing 0.9.3b)
circuit board: 11.5105cm x 5.74044cm
breadboards: 1

parts:
  LCM1602_IIC4 = LCM1602 IIC [part_number="LCM1602 IIC" chip_label="LCM1602 IIC" package="DIP (Dual Inline) [THT]"]
  LCD4 = LCD screen
  Part15 = FC-28 Soil Hygrometer Module - Probe
  Soil_Moisture = FC-28 Soil Hygrometer Module
  DHT3 = DHT22 Humidity and Temperature Sensor
  BH1750 = BH1750
  U2 = NodeMCU V1.0
  microSD2 = MicroSD Breakout
  R7 = Resistor [tolerance=±5% resistance=4.7k package=THT]
  Part13 = Barometric Pressure Sensor - BMP180 Breakout (GY-68)
  R8 = Resistor [tolerance=±5% resistance=4.7k package=THT]
  DS2 = DS18B20 1-Wire Temperature Sensor Probe Cable
  RTC = Tiny RTC - DS1307 Breakout Board

nets:
  VSS: LCM1602_IIC4.VSS, LCD4.VSS
  VDD: LCM1602_IIC4.VDD, LCD4.VDD
  N1: LCM1602_IIC4.V0, LCD4.V0
  N2: LCM1602_IIC4.RS, LCD4.RS
  N3: LCM1602_IIC4.RW, LCD4.R/W
  N4: LCM1602_IIC4.E, LCD4.E
  N5: LCM1602_IIC4.D0, LCD4.DB0
  N6: LCM1602_IIC4.D1, LCD4.DB1
  N7: LCM1602_IIC4.D2, LCD4.DB2
  N8: LCM1602_IIC4.D3, LCD4.DB3
  N9: LCM1602_IIC4.D4, LCD4.DB4
  N10: LCM1602_IIC4.D5, LCD4.DB5
  N11: LCM1602_IIC4.D6, LCD4.DB6
  N12: LCM1602_IIC4.D7, LCD4.DB7
  N13: LCM1602_IIC4.A, LCD4.LED+
  N14: LCM1602_IIC4.K, LCD4.LED-
  GND: LCM1602_IIC4.GND, Soil_Moisture.GND, DHT3.GND, BH1750.GND, U2.GND, microSD2.GND, Part13.GND, DS2.GND, RTC.GND
  VCC: LCM1602_IIC4.VCC, Soil_Moisture.VCC, DHT3.VDD, BH1750.VCC, U2.3V3, microSD2.3v, R7.Pin_1, Part13.VCC, R8.Pin_0, DS2.VDD, RTC.VCC
  N15: LCM1602_IIC4.SDA, BH1750.SDA, U2.D2, Part13.SDA, RTC.SDA
  N16: LCM1602_IIC4.SCL, BH1750.SCL, U2.D1, Part13.SCL, RTC.SCL
  N17: Part15.POS, Soil_Moisture.POS
  N18: Part15.NEG, Soil_Moisture.NEG
  N19: Soil_Moisture.AO, U2.A0
  N20: DHT3.DATA, U2.D4, R8.Pin_1
  N21: U2.D3, R7.Pin_0, DS2.DQ
  N22: U2.D5, microSD2.CLK
  N23: U2.D6, microSD2.DO
  N24: U2.D7, microSD2.DI
  N25: U2.D8, microSD2.CS

custom parts:
  LCM1602 IIC: I2C-Module to use a 1602 or 2004 LCD on with the wire.h libory Serial LCD Modul
  FC-28 Soil Hygrometer Module - Probe: The FC-28 is a soil hygrometer module that uses the Texas Instruments LM393 comparator chip to provide an analog measurement of soil humidity.
  FC-28 Soil Hygrometer Module: The FC-28 is a soil hygrometer module that uses the Texas Instruments LM393 comparator chip to provide an analog measurement of soil humidity. The digital output is high when soil moisture is over a certain threshold, as determined by adjusting the potentiometer.
  BH1750: Light Sensor
  NodeMCU V1.0: ESP8266 based NodeMCU
  MicroSD Breakout: 5V-ready microSD Breakout with Level Shifter
  Tiny RTC - DS1307 Breakout Board: The Tiny RTC is a breakout board for the Dallas Semiconductor/Maxim Integrated DS1307 real-time clock. The DS1307 counts seconds, minutes, hours, date of the month, month, day of the week, and year (with compensation for leap-years). The breakout board also has space for a DS18B20 digital thermometer.
